# Fritzing sketch Bluetooth-Comm (saved by Fritzing 0.8.7b)
breadboards: 1

parts:
  Part1 = Arduino Uno (Rev3)
  S1 = Pushbutton [package="[THT]"]
  R1 = Resistor [tolerance=±5% resistance=220 package=THT]
  S2 = Pushbutton [package="[THT]"]
  R2 = Resistor [tolerance=±5% resistance=220 package=THT]
  R3 = Resistor [tolerance=±5% resistance=220 package=THT]
  LED1 = LED - 5mm [color="Red (633nm)" package="5 mm [THT]"]
  LED2 = LED - 5mm [color="Red (633nm)" package="5 mm [THT]"]
  JY-MCU = JY-MCU

nets:
  N1: Part1.D10_PWM/SS, JY-MCU.GND
  N2: Part1.D11_PWM/MOSI, JY-MCU.VOC
  N3: Part1.D2, S2.Pin_1, S2.Pin_2, R2.Pin_0
  N4: Part1.D3_PWM, S1.Pin_1, S1.Pin_2, R1.Pin_0
  N5: Part1.D6_PWM, LED1.anode
  N6: Part1.D7, LED2.anode
  N7: Part1.5V, S1.Pin_3, S1.Pin_4, S2.Pin_3, S2.Pin_4, JY-MCU.RXD
  N8: Part1.GND, R1.Pin_1, R2.Pin_1, R3.Pin_1, JY-MCU.TXD
  N9: R3.Pin_0, LED1.cathode, LED2.cathode

notes:
  JY-MCU

custom parts:
  JY-MCU: Bluetooth
